# Fritzing sketch sketch (saved by Fritzing 0.9.3b)
breadboards: 1

parts:
  Bauteil1 = Matrix LED de 8x8 basada en MAX7219
  Bauteil2 = Matrix LED de 8x8 basada en MAX7219
  Bauteil3 = Matrix LED de 8x8 basada en MAX7219
  Bauteil4 = Matrix LED de 8x8 basada en MAX7219
  Bauteil5 = Matrix LED de 8x8 basada en MAX7219
  Bauteil6 = Matrix LED de 8x8 basada en MAX7219
  Bauteil7 = Matrix LED de 8x8 basada en MAX7219
  Bauteil8 = Matrix LED de 8x8 basada en MAX7219
  Bauteil9 = Matrix LED de 8x8 basada en MAX7219
  Bauteil10 = Matrix LED de 8x8 basada en MAX7219
  Bauteil11 = Matrix LED de 8x8 basada en MAX7219
  Bauteil12 = Matrix LED de 8x8 basada en MAX7219
  Bauteil13 = Matrix LED de 8x8 basada en MAX7219
  Bauteil14 = Matrix LED de 8x8 basada en MAX7219
  Bauteil15 = Matrix LED de 8x8 basada en MAX7219
  Bauteil16 = Matrix LED de 8x8 basada en MAX7219
  Bauteil18 = Matrix LED de 8x8 basada en MAX7219
  Bauteil19 = Matrix LED de 8x8 basada en MAX7219
  Bauteil20 = Matrix LED de 8x8 basada en MAX7219
  Bauteil22 = Matrix LED de 8x8 basada en MAX7219
  Bauteil23 = Matrix LED de 8x8 basada en MAX7219
  Bauteil24 = Matrix LED de 8x8 basada en MAX7219
  Bauteil26 = Matrix LED de 8x8 basada en MAX7219
  Bauteil27 = Matrix LED de 8x8 basada en MAX7219
  Bauteil28 = Matrix LED de 8x8 basada en MAX7219
  Bauteil30 = Matrix LED de 8x8 basada en MAX7219
  Bauteil31 = Matrix LED de 8x8 basada en MAX7219
  Bauteil32 = Matrix LED de 8x8 basada en MAX7219
  Bauteil33 = HY-SRF05 Ultrasonic Rangefinder
  Bauteil34 = HY-SRF05 Ultrasonic Rangefinder
  Raspberry_Pi_1 = Raspberry Pi 3 [part_number=RPI-3-V1.2]
  R3 = Resistor [tolerance=±5% resistance=520 package="2010 [SMD]"]
  R4 = Resistor [tolerance=±5% resistance=1k package="2010 [SMD]"]
  R2 = Resistor [tolerance=±5% resistance=1k package="2010 [SMD]"]
  R5 = Resistor [tolerance=±5% resistance=520 package="2010 [SMD]"]

nets:
  VCC: Bauteil1.VCC, Bauteil33.Vcc, Bauteil34.Vcc, Raspberry_Pi_1.5V
  GND: Bauteil1.GND#1, Bauteil33.GND, Bauteil34.GND, Raspberry_Pi_1.GND, R4.Pin_1, R2.Pin_1
  N1: Bauteil1.CS, Raspberry_Pi_1.GIPO8
  N2: Bauteil1.CLK, Raspberry_Pi_1.GIPO11
  N3: Bauteil1.DIN, Raspberry_Pi_1.3V3, Raspberry_Pi_1.GIPO10
  N4: Bauteil1.VCC(OUT), Bauteil2.VCC
  N5: Bauteil1.GND#6, Bauteil2.GND#1
  N6: Bauteil1.CS(OUT), Bauteil2.CS
  N7: Bauteil1.CLK(OUT), Bauteil2.CLK
  N8: Bauteil1.DOUT, Bauteil2.DIN
  N9: Bauteil2.VCC(OUT), Bauteil3.VCC
  N10: Bauteil2.GND#6, Bauteil3.GND#1
  N11: Bauteil2.CS(OUT), Bauteil3.CS
  N12: Bauteil2.CLK(OUT), Bauteil3.CLK
  N13: Bauteil2.DOUT, Bauteil3.DIN
  N14: Bauteil3.VCC(OUT), Bauteil4.VCC
  N15: Bauteil3.GND#6, Bauteil4.GND#1
  N16: Bauteil3.CS(OUT), Bauteil4.CS
  N17: Bauteil3.CLK(OUT), Bauteil4.CLK
  N18: Bauteil3.DOUT, Bauteil4.DIN
  N19: Bauteil4.VCC(OUT), Bauteil20.VCC
  N20: Bauteil4.GND#6, Bauteil20.GND#1
  N21: Bauteil4.CS(OUT), Bauteil20.CS
  N22: Bauteil4.CLK(OUT), Bauteil20.CLK
  N23: Bauteil4.DOUT, Bauteil20.DIN
  N24: Bauteil5.VCC, Bauteil6.VCC(OUT)
  N25: Bauteil5.GND#1, Bauteil6.GND#6
  N26: Bauteil5.CS, Bauteil6.CS(OUT)
  N27: Bauteil5.CLK, Bauteil6.CLK(OUT)
  N28: Bauteil5.DIN, Bauteil6.DOUT
  N29: Bauteil5.VCC(OUT), Bauteil24.VCC
  N30: Bauteil5.GND#6, Bauteil24.GND#1
  N31: Bauteil5.CS(OUT), Bauteil24.CS
  N32: Bauteil5.CLK(OUT), Bauteil24.CLK
  N33: Bauteil5.DOUT, Bauteil24.DIN
  N34: Bauteil6.VCC, Bauteil7.VCC(OUT)
  N35: Bauteil6.GND#1, Bauteil7.GND#6
  N36: Bauteil6.CS, Bauteil7.CS(OUT)
  N37: Bauteil6.CLK, Bauteil7.CLK(OUT)
  N38: Bauteil6.DIN, Bauteil7.DOUT
  N39: Bauteil7.VCC, Bauteil8.VCC(OUT)
  N40: Bauteil7.GND#1, Bauteil8.GND#6
  N41: Bauteil7.CS, Bauteil8.CS(OUT)
  N42: Bauteil7.CLK, Bauteil8.CLK(OUT)
  N43: Bauteil7.DIN, Bauteil8.DOUT
  N44: Bauteil8.VCC, Bauteil18.VCC(OUT)
  N45: Bauteil8.GND#1, Bauteil18.GND#6
  N46: Bauteil8.CS, Bauteil18.CS(OUT)
  N47: Bauteil8.CLK, Bauteil18.CLK(OUT)
  N48: Bauteil8.DIN, Bauteil18.DOUT
  N49: Bauteil9.VCC, Bauteil10.VCC(OUT)
  N50: Bauteil9.GND#1, Bauteil10.GND#6
  N51: Bauteil9.CS, Bauteil10.CS(OUT)
  N52: Bauteil9.CLK, Bauteil10.CLK(OUT)
  N53: Bauteil9.DIN, Bauteil10.DOUT
  N54: Bauteil9.VCC(OUT), Bauteil28.VCC
  N55: Bauteil9.GND#6, Bauteil28.GND#1
  N56: Bauteil9.CS(OUT), Bauteil28.CS
  N57: Bauteil9.CLK(OUT), Bauteil28.CLK
  N58: Bauteil9.DOUT, Bauteil28.DIN
  N59: Bauteil10.VCC, Bauteil11.VCC(OUT)
  N60: Bauteil10.GND#1, Bauteil11.GND#6
  N61: Bauteil10.CS, Bauteil11.CS(OUT)
  N62: Bauteil10.CLK, Bauteil11.CLK(OUT)
  N63: Bauteil10.DIN, Bauteil11.DOUT
  N64: Bauteil11.VCC, Bauteil12.VCC(OUT)
  N65: Bauteil11.GND#1, Bauteil12.GND#6
  N66: Bauteil11.CS, Bauteil12.CS(OUT)
  N67: Bauteil11.CLK, Bauteil12.CLK(OUT)
  N68: Bauteil11.DIN, Bauteil12.DOUT
  N69: Bauteil12.VCC, Bauteil22.VCC(OUT)
  N70: Bauteil12.GND#1, Bauteil22.GND#6
  N71: Bauteil12.CS, Bauteil22.CS(OUT)
  N72: Bauteil12.CLK, Bauteil22.CLK(OUT)
  N73: Bauteil12.DIN, Bauteil22.DOUT
  N74: Bauteil13.VCC, Bauteil14.VCC(OUT)
  N75: Bauteil13.GND#1, Bauteil14.GND#6
  N76: Bauteil13.CS, Bauteil14.CS(OUT)
  N77: Bauteil13.CLK, Bauteil14.CLK(OUT)
  N78: Bauteil13.DIN, Bauteil14.DOUT
  N79: Bauteil13.VCC(OUT), Bauteil32.VCC
  N80: Bauteil13.GND#6, Bauteil32.GND#1
  N81: Bauteil13.CS(OUT), Bauteil32.CS
  N82: Bauteil13.CLK(OUT), Bauteil32.CLK
  N83: Bauteil13.DOUT, Bauteil32.DIN
  N84: Bauteil14.VCC, Bauteil15.VCC(OUT)
  N85: Bauteil14.GND#1, Bauteil15.GND#6
  N86: Bauteil14.CS, Bauteil15.CS(OUT)
  N87: Bauteil14.CLK, Bauteil15.CLK(OUT)
  N88: Bauteil14.DIN, Bauteil15.DOUT
  N89: Bauteil15.VCC, Bauteil16.VCC(OUT)
  N90: Bauteil15.GND#1, Bauteil16.GND#6
  N91: Bauteil15.CS, Bauteil16.CS(OUT)
  N92: Bauteil15.CLK, Bauteil16.CLK(OUT)
  N93: Bauteil15.DIN, Bauteil16.DOUT
  N94: Bauteil16.VCC, Bauteil26.VCC(OUT)
  N95: Bauteil16.GND#1, Bauteil26.GND#6
  N96: Bauteil16.CS, Bauteil26.CS(OUT)
  N97: Bauteil16.CLK, Bauteil26.CLK(OUT)
  N98: Bauteil16.DIN, Bauteil26.DOUT
  N99: Bauteil18.VCC, Bauteil19.VCC(OUT)
  N100: Bauteil18.GND#1, Bauteil19.GND#6
  N101: Bauteil18.CS, Bauteil19.CS(OUT)
  N102: Bauteil18.CLK, Bauteil19.CLK(OUT)
  N103: Bauteil18.DIN, Bauteil19.DOUT
  N104: Bauteil19.VCC, Bauteil20.VCC(OUT)
  N105: Bauteil19.GND#1, Bauteil20.GND#6
  N106: Bauteil19.CS, Bauteil20.CS(OUT)
  N107: Bauteil19.CLK, Bauteil20.CLK(OUT)
  N108: Bauteil19.DIN, Bauteil20.DOUT
  N109: Bauteil22.VCC, Bauteil23.VCC(OUT)
  N110: Bauteil22.GND#1, Bauteil23.GND#6
  N111: Bauteil22.CS, Bauteil23.CS(OUT)
  N112: Bauteil22.CLK, Bauteil23.CLK(OUT)
  N113: Bauteil22.DIN, Bauteil23.DOUT
  N114: Bauteil23.VCC, Bauteil24.VCC(OUT)
  N115: Bauteil23.GND#1, Bauteil24.GND#6
  N116: Bauteil23.CS, Bauteil24.CS(OUT)
  N117: Bauteil23.CLK, Bauteil24.CLK(OUT)
  N118: Bauteil23.DIN, Bauteil24.DOUT
  N119: Bauteil26.VCC, Bauteil27.VCC(OUT)
  N120: Bauteil26.GND#1, Bauteil27.GND#6
  N121: Bauteil26.CS, Bauteil27.CS(OUT)
  N122: Bauteil26.CLK, Bauteil27.CLK(OUT)
  N123: Bauteil26.DIN, Bauteil27.DOUT
  N124: Bauteil27.VCC, Bauteil28.VCC(OUT)
  N125: Bauteil27.GND#1, Bauteil28.GND#6
  N126: Bauteil27.CS, Bauteil28.CS(OUT)
  N127: Bauteil27.CLK, Bauteil28.CLK(OUT)
  N128: Bauteil27.DIN, Bauteil28.DOUT
  N129: Bauteil30.VCC, Bauteil31.VCC(OUT)
  N130: Bauteil30.GND, Bauteil31.GND#6
  N131: Bauteil30.CS, Bauteil31.CS(OUT)
  N132: Bauteil30.CLK, Bauteil31.CLK(OUT)
  N133: Bauteil30.DIN, Bauteil31.DOUT
  N134: Bauteil31.VCC, Bauteil32.VCC(OUT)
  N135: Bauteil31.GND#1, Bauteil32.GND#6
  N136: Bauteil31.CS, Bauteil32.CS(OUT)
  N137: Bauteil31.CLK, Bauteil32.CLK(OUT)
  N138: Bauteil31.DIN, Bauteil32.DOUT
  N139: Bauteil33.Trig, Bauteil34.Trig, Raspberry_Pi_1.GIPO13, Raspberry_Pi_1.GIPO19
  N140: Bauteil33.Echo, R5.Pin_0
  N141: Bauteil34.Echo, R3.Pin_0
  N142: Raspberry_Pi_1.GIPO26, R3.Pin_1, R4.Pin_0
  N143: Raspberry_Pi_1.GIPO20, Raspberry_Pi_1.GIPO16, R2.Pin_0, R5.Pin_1
